# Fritzing sketch Untitled Sketch 2 (saved by Fritzing 0.9.3b)
breadboards: 1

parts:
  Holiday_Door_LED_Strip_Pi = Raspberry Pi 3 [part_number=RPI-3-V1.2]
  Red_Mosfet = Basic FET N-Channel [package="TO220 [THT]"]
  Q1 = Basic FET N-Channel [package="TO220 [THT]"]
  Button = Round Pushbutton
  SPKR1 = Loudspeaker  # not connected
  12V_Power_Supply = Battery
  LED_Strip_1 = DUO LED RG [package="5 mm [THT]"]
  LED_Strip_2 = DUO LED RG [package="5 mm [THT]"]

nets:
  N1: Holiday_Door_LED_Strip_Pi.GIPO4, Button.leg1
  N2: Holiday_Door_LED_Strip_Pi.GIPO13, Q1.gate
  N3: Holiday_Door_LED_Strip_Pi.GIPO12, Red_Mosfet.gate
  N4: Holiday_Door_LED_Strip_Pi.GND, Red_Mosfet.source, Q1.source, Button.leg0, 12V_Power_Supply.-
  N5: Q1.drain, LED_Strip_2.common_cathode
  N6: 12V_Power_Supply.+, LED_Strip_1.green_anode, LED_Strip_2.green_anode
